// Logisim project ALU.circ as structural Verilog: 1 circuit, main circuit main
module main (
  input  _1,
  input  _2,
  input  in_3,
  input  in_4,
  input  in_5,
  input  A,
  input  in_7,
  input  in_8,
  input  in_9,
  input  in_10,
  input  in_11,
  input  in_12,
  input  in_13,
  input  in_14,
  input  B,
  input  in_16,
  input  in_17,
  input  in_18,
  output out_19,
  output out_20,
  output out_21,
  output out_22,
  output OUT,
  output out_24,
  output out_25,
  output out_26,
  output A_B,
  output A_B_2,
  output A_B_3,
  output Out_is_null
);

  wire and_1_out, and_2_out, and_3_out, and_4_out, and_5_out, and_6_out, and_7_out, and_8_out, and_9_out,
       and_10_out, and_11_out, and_12_out, and_13_out, and_14_out, and_15_out, and_16_out, and_17_out,
       and_18_out, and_19_out, and_20_out, and_21_out, and_22_out, and_23_out, and_24_out, and_25_out,
       and_26_out, and_27_out, nand_1_out, nand_2_out, nand_3_out, nand_4_out, nand_5_out, nand_6_out,
       nand_7_out, nand_8_out, nand_9_out, nand_10_out, nand_11_out, nand_12_out, nand_13_out, nand_14_out,
       nand_15_out, nand_16_out, nand_17_out, nand_18_out, nand_19_out, nand_20_out, nand_21_out,
       nand_22_out, nand_23_out, nand_24_out, nand_25_out, nand_26_out, nand_27_out, nand_28_out,
       nand_29_out, nand_30_out, nand_31_out, nand_32_out, nand_33_out, nand_34_out, nand_35_out,
       nand_36_out, nand_37_out, nand_38_out, nand_39_out, nand_40_out, nand_41_out, nand_42_out,
       nand_43_out, nand_44_out, nand_45_out, nand_46_out, nand_47_out, nand_48_out, nand_49_out,
       nand_50_out, nand_51_out, nand_52_out, nand_53_out, nand_54_out, nand_55_out, nand_56_out,
       nand_57_out, nand_58_out, nand_59_out, nand_60_out, nor_1_out, nor_2_out, nor_3_out, nor_4_out,
       nor_5_out, nor_6_out, nor_7_out, nor_8_out, not_1_out, not_2_out, not_3_out, not_4_out, not_5_out,
       not_6_out, not_7_out, not_8_out, not_9_out, not_10_out, not_11_out, not_12_out, not_13_out,
       not_14_out, not_15_out, not_16_out, not_17_out, not_18_out, not_19_out, not_20_out, not_21_out,
       not_22_out, not_23_out, not_24_out, not_25_out, not_26_out, not_27_out, not_28_out, not_29_out,
       not_30_out, not_31_out, not_32_out, not_33_out, not_34_out, not_35_out, not_36_out, not_37_out,
       not_38_out, not_39_out, not_40_out, not_41_out, not_42_out, not_43_out, not_44_out, not_45_out,
       not_46_out, not_47_out, not_48_out, not_49_out, not_50_out, not_51_out, not_53_out, not_54_out,
       not_55_out, not_56_out, not_57_out, not_58_out, not_59_out, not_60_out, not_61_out, not_62_out,
       not_63_out, not_64_out, not_65_out, not_66_out, not_67_out, not_68_out, not_69_out, not_70_out,
       not_71_out, not_72_out, not_73_out, not_74_out, not_75_out, not_76_out, not_77_out, not_78_out,
       not_80_out, not_81_out, not_82_out, not_83_out, not_84_out, not_85_out, or_1_out, or_2_out, or_3_out,
       or_4_out, or_5_out, or_6_out, xnor_1_out, xnor_2_out, xnor_3_out, xnor_4_out, xnor_5_out, xnor_6_out,
       xnor_7_out, xnor_8_out, xor_1_out, xor_2_out, xor_3_out, xor_4_out, xor_5_out, xor_6_out, xor_7_out,
       xor_8_out, xor_9_out, xor_10_out, xor_11_out, xor_12_out, xor_13_out, xor_14_out, xor_15_out,
       xor_16_out, xor_17_out, xor_18_out, xor_19_out, xor_20_out, xor_21_out, xor_22_out;

  not not_1 (not_1_out, _1);
  not not_2 (not_2_out, _2);
  nand nand_1 (nand_1_out, not_1_out, not_2_out);
  not not_3 (not_3_out, nand_1_out);
  not not_4 (not_4_out, nand_2_out);
  nand nand_2 (nand_2_out, _1, not_2_out);
  nand nand_3 (nand_3_out, _2, not_1_out);
  not not_5 (not_5_out, nand_3_out);
  not not_6 (not_6_out, nand_4_out);
  nand nand_4 (nand_4_out, _1, _2);
  xor xor_1 (xor_1_out, in_12, not_4_out);
  xor xor_2 (xor_2_out, in_13, not_4_out);
  xor xor_3 (xor_3_out, in_14, not_4_out);
  xor xor_4 (xor_4_out, B, not_4_out);
  xor xor_5 (xor_5_out, in_16, not_4_out);
  xor xor_6 (xor_6_out, in_17, not_4_out);
  xor xor_7 (xor_7_out, in_3, in_11);
  xor xor_8 (xor_8_out, in_11, not_4_out);
  xor xor_9 (xor_9_out, in_4, in_12);
  xor xor_10 (xor_10_out, in_5, in_13);
  xor xor_11 (xor_11_out, A, in_14);
  xor xor_12 (xor_12_out, in_7, B);
  xor xor_13 (xor_13_out, in_8, in_16);
  xor xor_14 (xor_14_out, in_9, in_17);
  xor xor_15 (xor_15_out, in_10, in_18);
  and and_1 (and_1_out, xor_8_out, in_3);
  and and_2 (and_2_out, in_4, and_1_out);
  and and_3 (and_3_out, xor_1_out, and_1_out);
  and and_4 (and_4_out, xor_1_out, in_4);
  and and_5 (and_5_out, in_5, or_1_out);
  and and_6 (and_6_out, xor_2_out, or_1_out);
  and and_7 (and_7_out, xor_2_out, in_5);
  and and_8 (and_8_out, A, or_2_out);
  and and_9 (and_9_out, xor_3_out, or_2_out);
  and and_10 (and_10_out, xor_3_out, A);
  and and_11 (and_11_out, in_7, or_3_out);
  and and_12 (and_12_out, xor_4_out, or_3_out);
  and and_13 (and_13_out, xor_4_out, in_7);
  and and_14 (and_14_out, in_8, or_4_out);
  and and_15 (and_15_out, xor_5_out, or_4_out);
  and and_16 (and_16_out, xor_5_out, in_8);
  and and_17 (and_17_out, in_9, or_5_out);
  and and_18 (and_18_out, xor_6_out, or_5_out);
  and and_19 (and_19_out, xor_6_out, in_9);
  xor xor_16 (xor_16_out, and_1_out, xor_9_out);
  xor xor_17 (xor_17_out, or_1_out, xor_10_out);
  xor xor_18 (xor_18_out, or_2_out, xor_11_out);
  xor xor_19 (xor_19_out, or_3_out, xor_12_out);
  xor xor_20 (xor_20_out, or_4_out, xor_13_out);
  xor xor_21 (xor_21_out, or_5_out, xor_14_out);
  xor xor_22 (xor_22_out, or_6_out, xor_15_out);
  or or_1 (or_1_out, and_2_out, and_3_out, and_4_out);
  or or_2 (or_2_out, and_5_out, and_6_out, and_7_out);
  or or_3 (or_3_out, and_8_out, and_9_out, and_10_out);
  or or_4 (or_4_out, and_11_out, and_12_out, and_13_out);
  or or_5 (or_5_out, and_14_out, and_15_out, and_16_out);
  or or_6 (or_6_out, and_17_out, and_18_out, and_19_out);
  nor nor_1 (nor_1_out, not_4_out, not_3_out);
  not not_7 (not_7_out, nor_1_out);
  not not_8 (not_8_out, nand_5_out);
  nand nand_5 (nand_5_out, xor_7_out, not_7_out);
  nand nand_6 (nand_6_out, xor_16_out, not_7_out);
  not not_9 (not_9_out, nand_6_out);
  nand nand_7 (nand_7_out, xor_17_out, not_7_out);
  not not_10 (not_10_out, nand_7_out);
  nand nand_8 (nand_8_out, xor_18_out, not_7_out);
  not not_11 (not_11_out, nand_8_out);
  nand nand_9 (nand_9_out, xor_19_out, not_7_out);
  not not_12 (not_12_out, nand_9_out);
  nand nand_10 (nand_10_out, xor_20_out, not_7_out);
  not not_13 (not_13_out, nand_10_out);
  nand nand_11 (nand_11_out, xor_21_out, not_7_out);
  not not_14 (not_14_out, nand_11_out);
  nand nand_12 (nand_12_out, xor_22_out, not_7_out);
  not not_15 (not_15_out, nand_12_out);
  or or_7 (out_19, not_8_out, not_16_out, 1'b0);
  or or_8 (out_20, not_9_out, not_17_out, not_23_out);
  or or_9 (out_21, not_10_out, not_18_out, not_24_out);
  or or_10 (out_22, not_11_out, not_19_out, not_25_out);
  or or_11 (OUT, not_12_out, not_20_out, not_26_out);
  or or_12 (out_24, not_13_out, not_21_out, not_27_out);
  or or_13 (out_25, not_14_out, not_22_out, not_28_out);
  or or_14 (out_26, not_15_out, 1'b0, not_29_out);
  not not_16 (not_16_out, nand_13_out);
  nand nand_13 (nand_13_out, not_5_out, in_4);
  nand nand_14 (nand_14_out, not_5_out, in_5);
  not not_17 (not_17_out, nand_14_out);
  nand nand_15 (nand_15_out, not_5_out, A);
  not not_18 (not_18_out, nand_15_out);
  nand nand_16 (nand_16_out, not_5_out, in_7);
  not not_19 (not_19_out, nand_16_out);
  nand nand_17 (nand_17_out, not_5_out, in_8);
  not not_20 (not_20_out, nand_17_out);
  not not_21 (not_21_out, nand_18_out);
  nand nand_18 (nand_18_out, not_5_out, in_9);
  not not_22 (not_22_out, nand_19_out);
  nand nand_19 (nand_19_out, not_5_out, in_10);
  not not_23 (not_23_out, nand_20_out);
  nand nand_20 (nand_20_out, not_6_out, in_3);
  not not_24 (not_24_out, nand_21_out);
  nand nand_21 (nand_21_out, not_6_out, in_4);
  not not_25 (not_25_out, nand_22_out);
  nand nand_22 (nand_22_out, not_6_out, in_5);
  not not_26 (not_26_out, nand_23_out);
  nand nand_23 (nand_23_out, not_6_out, A);
  nand nand_24 (nand_24_out, not_6_out, in_7);
  not not_27 (not_27_out, nand_24_out);
  not not_28 (not_28_out, nand_25_out);
  nand nand_25 (nand_25_out, not_6_out, in_8);
  not not_29 (not_29_out, nand_26_out);
  nand nand_26 (nand_26_out, not_6_out, in_9);
  not not_30 (not_30_out, not_8_out);
  not not_31 (not_31_out, not_9_out);
  not not_32 (not_32_out, not_10_out);
  not not_33 (not_33_out, not_11_out);
  not not_34 (not_34_out, not_12_out);
  not not_35 (not_35_out, not_13_out);
  not not_36 (not_36_out, not_14_out);
  not not_37 (not_37_out, not_15_out);
  nand nand_27 (nand_27_out, not_30_out, not_31_out);
  nand nand_28 (nand_28_out, not_32_out, not_33_out);
  nand nand_29 (nand_29_out, not_34_out, not_35_out);
  nand nand_30 (nand_30_out, not_36_out, not_37_out);
  not not_38 (not_38_out, in_11);
  not not_39 (not_39_out, in_12);
  not not_40 (not_40_out, in_13);
  not not_41 (not_41_out, in_14);
  not not_42 (not_42_out, B);
  not not_43 (not_43_out, in_16);
  not not_44 (not_44_out, in_17);
  not not_45 (not_45_out, in_18);
  not not_46 (not_46_out, nand_27_out);
  not not_47 (not_47_out, nand_28_out);
  not not_48 (not_48_out, nand_29_out);
  not not_49 (not_49_out, nand_30_out);
  xnor xnor_1 (xnor_1_out, in_3, in_11);
  and and_20 (and_20_out, in_3, not_38_out);
  xnor xnor_2 (xnor_2_out, in_4, in_12);
  and and_21 (and_21_out, in_4, not_39_out);
  xnor xnor_3 (xnor_3_out, in_5, in_13);
  and and_22 (and_22_out, in_5, not_40_out);
  xnor xnor_4 (xnor_4_out, A, in_14);
  and and_23 (and_23_out, A, not_41_out);
  xnor xnor_5 (xnor_5_out, in_7, B);
  and and_24 (and_24_out, in_7, not_42_out);
  xnor xnor_6 (xnor_6_out, in_8, in_16);
  and and_25 (and_25_out, in_8, not_43_out);
  xnor xnor_7 (xnor_7_out, in_9, in_17);
  and and_26 (and_26_out, in_9, not_44_out);
  xnor xnor_8 (xnor_8_out, in_10, in_18);
  and and_27 (and_27_out, in_10, not_45_out);
  not not_50 (not_50_out, nand_31_out);
  nand nand_31 (nand_31_out, not_46_out, not_47_out);
  nand nand_32 (nand_32_out, not_48_out, not_49_out);
  not not_51 (not_51_out, nand_32_out);
  not not_52 (Out_is_null, nand_33_out);
  nand nand_33 (nand_33_out, not_50_out, not_51_out);
  nand nand_34 (nand_34_out, xnor_1_out, xnor_2_out);
  nand nand_35 (nand_35_out, xnor_3_out, xnor_4_out);
  nand nand_36 (nand_36_out, xnor_5_out, xnor_6_out);
  nand nand_37 (nand_37_out, xnor_7_out, xnor_8_out);
  nand nand_38 (nand_38_out, and_20_out, xnor_2_out);
  nand nand_39 (nand_39_out, xnor_3_out, xnor_4_out, xnor_5_out);
  nand nand_40 (nand_40_out, xnor_6_out, xnor_7_out, xnor_8_out, xnor_8_out);
  nand nand_41 (nand_41_out, and_21_out, xnor_3_out);
  nand nand_42 (nand_42_out, xnor_4_out, xnor_5_out, xnor_6_out);
  nand nand_43 (nand_43_out, xnor_7_out, xnor_8_out);
  nand nand_44 (nand_44_out, and_22_out, xnor_4_out);
  nand nand_45 (nand_45_out, xnor_5_out, xnor_6_out);
  nand nand_46 (nand_46_out, xnor_7_out, xnor_8_out);
  nand nand_47 (nand_47_out, and_23_out, xnor_6_out, xnor_5_out);
  nand nand_48 (nand_48_out, xnor_7_out, xnor_7_out, xnor_8_out);
  nand nand_49 (nand_49_out, and_24_out, xnor_6_out);
  nand nand_50 (nand_50_out, xnor_7_out, xnor_7_out, xnor_7_out);
  nand nand_51 (nand_51_out, and_25_out, xnor_7_out, xnor_8_out);
  nand nand_52 (nand_52_out, and_26_out, xnor_8_out);
  not not_53 (not_53_out, nand_34_out);
  not not_54 (not_54_out, nand_35_out);
  not not_55 (not_55_out, nand_36_out);
  not not_56 (not_56_out, nand_37_out);
  not not_57 (not_57_out, nand_38_out);
  not not_58 (not_58_out, nand_39_out);
  not not_59 (not_59_out, nand_40_out);
  not not_60 (not_60_out, nand_41_out);
  not not_61 (not_61_out, nand_42_out);
  not not_62 (not_62_out, nand_43_out);
  not not_63 (not_63_out, nand_44_out);
  not not_64 (not_64_out, nand_45_out);
  not not_65 (not_65_out, nand_46_out);
  not not_66 (not_66_out, nand_47_out);
  not not_67 (not_67_out, nand_48_out);
  not not_68 (not_68_out, nand_49_out);
  not not_69 (not_69_out, nand_50_out);
  not not_70 (not_70_out, nand_51_out);
  not not_71 (not_71_out, nand_52_out);
  nand nand_53 (nand_53_out, not_53_out, not_54_out);
  nand nand_54 (nand_54_out, not_55_out, not_56_out);
  nand nand_55 (nand_55_out, not_57_out, not_58_out, not_59_out);
  nand nand_56 (nand_56_out, not_60_out, not_61_out, not_62_out);
  nand nand_57 (nand_57_out, not_63_out, not_64_out, not_65_out);
  nand nand_58 (nand_58_out, not_66_out, not_67_out);
  nand nand_59 (nand_59_out, not_68_out, not_69_out);
  not not_72 (not_72_out, nand_53_out);
  not not_73 (not_73_out, nand_54_out);
  not not_74 (not_74_out, nand_55_out);
  not not_75 (not_75_out, nand_56_out);
  not not_76 (not_76_out, nand_57_out);
  not not_77 (not_77_out, nand_58_out);
  not not_78 (not_78_out, nand_59_out);
  not not_79 (A_B, nand_60_out);
  nand nand_60 (nand_60_out, not_72_out, not_73_out);
  not not_80 (not_80_out, nor_2_out);
  nor nor_2 (nor_2_out, not_74_out, not_75_out);
  nor nor_3 (nor_3_out, not_76_out, not_77_out);
  not not_81 (not_81_out, nor_3_out);
  nor nor_4 (nor_4_out, not_78_out, not_70_out);
  not not_82 (not_82_out, nor_4_out);
  not not_83 (not_83_out, nor_5_out);
  nor nor_5 (nor_5_out, not_71_out, not_71_out, and_27_out);
  nor nor_6 (nor_6_out, not_80_out, not_81_out);
  not not_84 (not_84_out, nor_6_out);
  nor nor_7 (nor_7_out, not_82_out, not_83_out);
  not not_85 (not_85_out, nor_7_out);
  not not_86 (A_B_3, nor_8_out);
  nor nor_8 (nor_8_out, not_84_out, not_85_out);
  nor nor_9 (A_B_2, A_B, A_B_3);

  // Notes on the sheet:
  //   MODE
  //   a-1
  //   b-1
  //   a-2
  //   b-2
  //   a-3
  //   b-3
  //   a-5
  //   b-5
  //   b-6
  //   b-2
  //   diff
  //   b-3
  //   diff
  //   a-4
  //   b-4
  //   b-4
  //   diff
  //   b-5
  //   diff
  //   a-6
  //   b-6
  //   diff
  //   a-7
  //   b-7
  //   b-7
  //   diff
  //   a-8
  //   b-8
  //   b-1
  //   diff
  //   xti-2
  //   Сдвиг в право на 1 разряд
  //   Сумматор/Вычитатель
  //   a-1
  //   xti-1
  //   xto-1
  //   om-1
  //   xto-1
  //   a-2
  //   xto-2
  //   om-2
  //   xto-2
  //   a-3
  //   xti-3
  //   xto-3
  //   om-3
  //   xto-3
  //   a-4
  //   xti-4
  //   xto-4
  //   om-4
  //   xto-4
  //   a-5
  //   xti-5
  //   xto-5
  //   om-5
  //   xto-5
  //   a-6
  //   xti-6
  //   xto-6
  //   om-6
  //   xto-6
  //   a-7
  //   xti-7
  //   xto-7
  //   om-7
  //   Сдвиг влево на 1 разряд
  //   xto-1
  //   o-1
  //   o-2
  //   xto-2
  //   o-3
  //   xto-3
  //   o-4
  //   xto-4
  //   o-5
  //   xto-5
  //   o-6
  //   xto-6
  //   o-7
  //   xto-7
  //   o-8
  //   Компаратор (>/</=)
endmodule
