// Logisim project CU.circ as structural Verilog: 1 circuit, main circuit main
module main (
  input  _3,
  input  _2,
  input  _1,
  input  _0,
  input  A___B,
  input  A___B_2,
  input  A___B_3,
  input  Result_is_null,
  input  Set_1,
  input  Reset,
  output \EN_СК ,
  output \HS_СК ,
  output \EN_ОЗУ ,
  output \RW_ОЗУ ,
  output \EN_РКК ,
  output \RW_РКК ,
  output \EN_РA ,
  output RW_PA,
  output \EN_РB ,
  output \RW_РB ,
  output \EN_РP ,
  output \RW_РP ,
  output \EN_РПА ,
  output \RW_РПА ,
  output \АЛУ_1_бит ,
  output out_26,
  output \EN_АЛУ ,
  output \EN_РФ ,
  output \RW_РФ 
);

  wire and_1_out, and_2_out, and_3_out, and_4_out, and_5_out, and_6_out, and_7_out, and_8_out, and_9_out,
       and_10_out, and_11_out, and_12_out, and_13_out, and_14_out, and_15_out, and_16_out, and_17_out,
       and_18_out, and_19_out, and_20_out, and_21_out, and_22_out, and_23_out, and_24_out, and_25_out,
       and_26_out, and_27_out, and_28_out, and_29_out, and_30_out, and_31_out, and_32_out, and_33_out,
       and_34_out, and_35_out, and_36_out, and_37_out, and_38_out, and_39_out, and_40_out, and_41_out,
       and_42_out, and_43_out, and_44_out, and_45_out, and_46_out, and_47_out, and_48_out, and_49_out,
       and_50_out, and_51_out, and_52_out, and_53_out, and_54_out, and_55_out, and_56_out, and_57_out,
       and_58_out, and_59_out, and_60_out, and_61_out, and_62_out, and_63_out, and_64_out, and_65_out,
       and_66_out, and_67_out, and_68_out, and_69_out, and_70_out, and_71_out, and_72_out, and_73_out,
       and_74_out, and_75_out, and_76_out, and_77_out, and_78_out, and_79_out, and_80_out, and_81_out,
       and_82_out, and_83_out, and_84_out, and_85_out, and_86_out, and_87_out, and_88_out, and_89_out,
       and_90_out, and_91_out, and_92_out, and_93_out, and_94_out, and_95_out, and_96_out, and_97_out,
       and_98_out, and_99_out, and_100_out, and_101_out, and_102_out, and_103_out, and_104_out, and_105_out,
       and_106_out, and_107_out, and_108_out, and_109_out, and_110_out, and_111_out, and_112_out,
       and_113_out, and_114_out, and_115_out, and_116_out, and_117_out, and_118_out, and_119_out,
       and_120_out, and_121_out, and_122_out, and_123_out, and_124_out, and_125_out, and_126_out,
       and_127_out, and_128_out, and_129_out, and_130_out, and_131_out, and_132_out, and_133_out,
       and_134_out, and_135_out, and_136_out, and_137_out, and_138_out, and_139_out, and_140_out,
       and_141_out, and_142_out, and_143_out, and_144_out, and_145_out, and_146_out, and_147_out,
       and_148_out, and_149_out, and_150_out, and_151_out, and_152_out, and_153_out, and_154_out,
       and_155_out, and_156_out, and_157_out, and_158_out, and_159_out, and_160_out, and_161_out,
       and_162_out, and_163_out, and_164_out, and_165_out, and_166_out, and_167_out, and_168_out,
       and_169_out, and_170_out, and_171_out, and_172_out, and_173_out, and_174_out, and_175_out,
       and_176_out, and_177_out, and_178_out, and_179_out, and_180_out, and_181_out, and_182_out,
       and_183_out, and_184_out, and_185_out, and_186_out, and_187_out, and_188_out, and_189_out,
       and_190_out, and_191_out, and_192_out, and_193_out, and_194_out, and_195_out, and_196_out,
       and_197_out, and_198_out, and_199_out, and_200_out, and_201_out, and_202_out, and_203_out,
       and_204_out, and_205_out, and_206_out, and_207_out, and_208_out, and_209_out, and_210_out,
       and_211_out, and_212_out, and_213_out, and_214_out, and_215_out, and_216_out, and_217_out,
       and_218_out, and_219_out, and_220_out, and_221_out, and_222_out, and_223_out, and_224_out,
       and_225_out, and_226_out, and_227_out, and_228_out, and_229_out, and_230_out, and_231_out,
       and_232_out, and_233_out, and_234_out, and_235_out, and_236_out, and_237_out, and_238_out,
       and_239_out, and_240_out, and_241_out, and_242_out, and_243_out, and_244_out, and_245_out,
       and_246_out, and_247_out, and_248_out, and_249_out, and_250_out, and_251_out, and_252_out,
       and_253_out, and_254_out, and_255_out, and_256_out, and_257_out, and_258_out, and_259_out,
       clock_1_out, d_ff_1_q, d_ff_2_q, d_ff_3_q, d_ff_4_q, d_ff_5_q, nand_1_out, nand_2_out, nand_3_out,
       nand_4_out, nand_5_out, nand_6_out, nand_7_out, nand_8_out, nand_9_out, nand_10_out, nand_11_out,
       nand_12_out, nand_13_out, nand_14_out, nand_15_out, nand_16_out, nor_1_out, nor_2_out, nor_3_out,
       nor_4_out, nor_5_out, nor_6_out, nor_7_out, nor_8_out, nor_9_out, not_1_out, not_2_out, not_3_out,
       not_4_out, not_5_out, or_20_out, or_21_out, or_22_out, or_23_out, or_24_out, or_25_out, or_26_out,
       or_27_out, or_28_out, or_29_out, or_30_out, or_31_out, or_32_out, or_33_out, or_34_out, or_35_out,
       or_36_out, or_37_out, or_38_out, or_39_out, or_40_out, or_41_out, or_42_out, or_43_out, or_44_out,
       or_45_out, or_46_out, or_47_out, or_48_out, or_49_out, or_50_out, or_51_out, or_52_out, or_53_out,
       or_54_out, or_55_out, or_56_out, or_57_out, or_58_out, or_59_out, or_60_out, or_61_out, or_62_out,
       or_63_out, or_64_out, or_65_out, or_66_out, or_67_out, or_68_out, or_69_out, or_70_out, or_71_out,
       or_72_out, or_73_out, or_74_out, or_75_out, or_76_out, or_77_out, or_78_out, or_79_out, or_80_out,
       or_81_out, or_82_out, or_83_out, or_84_out, or_85_out, or_86_out, or_87_out, or_88_out, or_89_out,
       or_90_out, or_91_out, or_92_out, or_93_out, or_94_out, or_95_out, or_96_out, or_97_out, or_98_out,
       or_99_out, or_100_out, or_101_out, or_102_out, or_103_out, or_104_out, or_105_out, or_106_out,
       or_107_out, or_108_out, or_109_out, or_110_out, or_111_out, or_112_out, or_113_out, or_114_out,
       or_115_out, or_116_out, or_117_out, or_118_out, or_119_out, or_120_out, or_121_out, or_122_out,
       or_123_out, or_124_out, or_125_out, or_126_out, or_127_out, or_128_out, or_129_out, or_130_out,
       or_131_out, or_132_out, or_133_out, or_134_out, or_135_out, or_136_out, or_137_out, or_138_out,
       or_139_out, or_140_out, or_141_out, or_142_out, or_143_out, or_144_out, or_145_out, or_146_out,
       or_147_out, or_148_out, or_149_out, or_150_out, or_151_out, or_152_out, or_153_out, or_154_out,
       or_155_out, or_156_out, undriven, undriven_2, undriven_3, undriven_4, undriven_5, undriven_6,
       undriven_7, undriven_8, undriven_9, undriven_10, undriven_11, undriven_12, undriven_13, undriven_14,
       undriven_15, undriven_16, undriven_17, undriven_18, undriven_19, undriven_20, undriven_21,
       undriven_22, undriven_23, undriven_24, undriven_25, undriven_26, undriven_27, undriven_28,
       undriven_29, undriven_30, undriven_31, undriven_32, undriven_33, undriven_34, undriven_35,
       undriven_36, undriven_37, undriven_38, undriven_39, undriven_40, undriven_41, undriven_42,
       undriven_43, undriven_44, undriven_45, undriven_46, undriven_47, undriven_48, undriven_49,
       undriven_50, undriven_51, undriven_52, undriven_53, undriven_54, undriven_55, undriven_56,
       undriven_57, undriven_58, undriven_59, undriven_60, undriven_61, undriven_62, undriven_63,
       undriven_64, undriven_65, undriven_66, undriven_67, undriven_68, undriven_69, undriven_70,
       undriven_71, undriven_72, undriven_73, undriven_74, undriven_75, undriven_76, undriven_77,
       undriven_78, undriven_79, undriven_80, undriven_81, undriven_82, undriven_83, undriven_84,
       undriven_85, undriven_86, undriven_87, undriven_88, undriven_89, undriven_90, undriven_91,
       undriven_92, undriven_93, undriven_94, undriven_95, undriven_96, undriven_97, undriven_98,
       undriven_99, undriven_100, undriven_101, undriven_102, undriven_103, undriven_104, undriven_105,
       undriven_106, undriven_107, undriven_108, undriven_109, undriven_110, undriven_111, undriven_112,
       undriven_113, undriven_114;

  Clock clock_1 (.out(clock_1_out));
  D_Flip_Flop d_ff_1 (.clk(clock_1_out), .D(d_ff_5_q), .Q(d_ff_1_q), .preset(Set_1), .reset(Reset));  // open: Qn, en
  D_Flip_Flop d_ff_2 (.clk(clock_1_out), .D(d_ff_1_q), .Q(d_ff_2_q), .reset(Reset));  // open: Qn, preset, en
  D_Flip_Flop d_ff_3 (.clk(clock_1_out), .D(d_ff_2_q), .Q(d_ff_3_q), .reset(Reset));  // open: Qn, preset, en
  D_Flip_Flop d_ff_4 (.clk(clock_1_out), .D(d_ff_3_q), .Q(d_ff_4_q), .reset(Reset));  // open: Qn, preset, en
  D_Flip_Flop d_ff_5 (.clk(clock_1_out), .D(d_ff_4_q), .Q(d_ff_5_q), .reset(Reset));  // open: Qn, preset, en
  or or_1 (\EN_СК , or_20_out, or_21_out, or_22_out);
  or or_2 (\HS_СК , or_23_out, or_24_out, or_25_out);
  or or_3 (\EN_ОЗУ , or_26_out, or_27_out, or_28_out);
  or or_4 (\RW_ОЗУ , or_29_out, or_30_out, or_31_out);
  or or_5 (\EN_РКК , or_32_out, or_33_out, or_34_out);
  or or_6 (\RW_РКК , or_35_out, or_36_out, or_37_out);
  or or_7 (\EN_РA , or_38_out, or_39_out, or_40_out);
  or or_8 (RW_PA, or_41_out, or_42_out, or_43_out);
  or or_9 (\EN_РB , or_44_out, or_45_out, or_46_out);
  or or_10 (\RW_РB , or_47_out, or_48_out, or_49_out);
  or or_11 (\EN_РP , or_50_out, or_51_out, or_52_out);
  or or_12 (\RW_РP , or_53_out, or_54_out, or_55_out);
  or or_13 (\EN_РПА , or_56_out, or_57_out, or_58_out);
  or or_14 (\RW_РПА , or_59_out, or_60_out, or_61_out);
  or or_15 (\АЛУ_1_бит , or_62_out, or_63_out, or_64_out);
  or or_16 (out_26, or_65_out, or_66_out, or_67_out);
  or or_17 (\EN_АЛУ , or_68_out, or_69_out, or_70_out);
  or or_18 (\EN_РФ , or_71_out, or_72_out, or_73_out);
  or or_19 (\RW_РФ , or_74_out, or_75_out, or_76_out);
  or or_20 (or_20_out, and_17_out, and_18_out, and_19_out, and_20_out);
  or or_21 (or_21_out, and_29_out, and_30_out, and_33_out, and_34_out);
  or or_22 (or_22_out, and_35_out, and_36_out);
  or or_23 (or_23_out, and_22_out, and_24_out, and_26_out, and_27_out);
  or or_24 (or_24_out, and_28_out, and_31_out, and_32_out, and_48_out);
  or or_25 (or_25_out, and_50_out, and_52_out);
  or or_26 (or_26_out, and_23_out, and_25_out, and_41_out, and_44_out);
  or or_27 (or_27_out, and_45_out, and_46_out, and_47_out, and_49_out);
  or or_28 (or_28_out, and_51_out, and_68_out);
  or or_29 (or_29_out, and_39_out, and_40_out, and_42_out, and_43_out);
  or or_30 (or_30_out, and_61_out, and_62_out, and_65_out, and_66_out);
  or or_31 (or_31_out, and_67_out, and_69_out);
  or or_32 (or_32_out, and_38_out, and_56_out, and_57_out, and_59_out);
  or or_33 (or_33_out, and_60_out, and_63_out, and_64_out, and_81_out);
  or or_34 (or_34_out, and_83_out, and_85_out);
  or or_35 (or_35_out, and_54_out, and_55_out, and_58_out, and_75_out);
  or or_36 (or_36_out, and_77_out, and_79_out, and_80_out, and_82_out);
  or or_37 (or_37_out, and_84_out, and_86_out);
  or or_38 (or_38_out, and_71_out, and_73_out, and_74_out, and_76_out);
  or or_39 (or_39_out, and_78_out, and_96_out, and_99_out, and_101_out);
  or or_40 (or_40_out, and_102_out, and_103_out);
  or or_41 (or_41_out, and_72_out, and_90_out, and_92_out, and_93_out);
  or or_42 (or_42_out, and_95_out, and_97_out, and_98_out, and_100_out);
  or or_43 (or_43_out, and_118_out, and_120_out);
  or or_44 (or_44_out, and_88_out, and_89_out, and_91_out, and_94_out);
  or or_45 (or_45_out, and_110_out, and_113_out, and_114_out, and_116_out);
  or or_46 (or_46_out, and_117_out, and_119_out);
  or or_47 (or_47_out, and_105_out, and_107_out, and_108_out, and_109_out);
  or or_48 (or_48_out, and_111_out, and_112_out, and_115_out, and_131_out);
  or or_49 (or_49_out, and_133_out, and_135_out);
  or or_50 (or_50_out, and_104_out, and_106_out, and_125_out, and_126_out);
  or or_51 (or_51_out, and_128_out, and_129_out, and_130_out, and_132_out);
  or or_52 (or_52_out, and_134_out, and_150_out);
  or or_53 (or_53_out, and_121_out, and_123_out, and_124_out, and_127_out);
  or or_54 (or_54_out, and_142_out, and_144_out, and_147_out, and_148_out);
  or or_55 (or_55_out, and_149_out, and_151_out);
  or or_56 (or_56_out, and_122_out, and_137_out, and_140_out, and_141_out);
  or or_57 (or_57_out, and_143_out, and_145_out, and_146_out, and_162_out);
  or or_58 (or_58_out, and_164_out, and_167_out);
  or or_59 (or_59_out, and_136_out, and_138_out, and_139_out, and_156_out);
  or or_60 (or_60_out, and_158_out, and_160_out, and_161_out, and_163_out);
  or or_61 (or_61_out, and_165_out, and_166_out);
  or or_62 (or_62_out, and_153_out, and_154_out, and_155_out, and_157_out);
  or or_63 (or_63_out, and_159_out, and_177_out, and_178_out, and_181_out);
  or or_64 (or_64_out, and_182_out, and_183_out);
  or or_65 (or_65_out, and_152_out, and_169_out, and_171_out, and_174_out);
  or or_66 (or_66_out, and_175_out, and_176_out, and_179_out, and_180_out);
  or or_67 (or_67_out, and_197_out, and_199_out);
  or or_68 (or_68_out, and_168_out, and_170_out, and_172_out, and_173_out);
  or or_69 (or_69_out, and_190_out, and_192_out, and_194_out, and_196_out);
  or or_70 (or_70_out, and_198_out, and_200_out);
  or or_71 (or_71_out, and_185_out, and_187_out, and_188_out, and_189_out);
  or or_72 (or_72_out, and_191_out, and_193_out, and_195_out, and_207_out);
  or or_73 (or_73_out, and_209_out, and_210_out);
  or or_74 (or_74_out, and_184_out, and_186_out, and_201_out, and_202_out);
  or or_75 (or_75_out, and_203_out, and_204_out, and_205_out, and_206_out);
  or or_76 (or_76_out, and_208_out, and_219_out);
  not not_1 (not_1_out, _1);
  and and_1 (and_1_out, not_1_out, _0);
  nor nor_1 (nor_1_out, _3, _2);
  and and_2 (and_2_out, nor_1_out, and_1_out);
  and and_3 (and_3_out, _1, not_2_out);
  nor nor_2 (nor_2_out, _3, _2);
  and and_4 (and_4_out, nor_2_out, and_3_out);
  not not_2 (not_2_out, _0);
  and and_5 (and_5_out, _1, _0);
  nor nor_3 (nor_3_out, _3, _2);
  and and_6 (and_6_out, nor_3_out, and_5_out);
  not not_3 (not_3_out, _1);
  and and_7 (and_7_out, not_3_out, _2);
  nor nor_4 (nor_4_out, _1, _0);
  and and_8 (and_8_out, nor_4_out, and_7_out);
  nor nor_5 (nor_5_out, _3, _1);
  and and_9 (and_9_out, _2, _0);
  and and_10 (and_10_out, nor_5_out, and_9_out);
  nor nor_6 (nor_6_out, _3, _0);
  and and_11 (and_11_out, _2, _1);
  and and_12 (and_12_out, nor_6_out, and_11_out);
  not not_4 (not_4_out, _3);
  and and_13 (and_13_out, not_4_out, _2);
  and and_14 (and_14_out, _1, _0);
  and and_15 (and_15_out, and_13_out, and_14_out);
  nor nor_7 (nor_7_out, _1, _0);
  and and_16 (and_16_out, nor_7_out, and_21_out);
  or or_77 (or_77_out, and_211_out, and_213_out, and_216_out, and_217_out);
  or or_78 (or_78_out, and_211_out, and_213_out, and_215_out, and_218_out);
  and and_17 (and_17_out, or_78_out, and_2_out);
  and and_18 (and_18_out, or_98_out, and_4_out);
  and and_19 (and_19_out, or_118_out, and_6_out);
  and and_20 (and_20_out, or_138_out, and_8_out);
  not not_5 (not_5_out, _2);
  and and_21 (and_21_out, not_5_out, _3);
  or or_79 (or_79_out, and_212_out, and_213_out, and_216_out, and_217_out);
  and and_22 (and_22_out, or_77_out, and_2_out);
  and and_23 (and_23_out, or_79_out, and_2_out);
  and and_24 (and_24_out, or_97_out, and_4_out);
  and and_25 (and_25_out, or_99_out, and_4_out);
  and and_26 (and_26_out, or_117_out, and_6_out);
  and and_27 (and_27_out, or_137_out, and_8_out);
  and and_28 (and_28_out, undriven_6, and_10_out);
  and and_29 (and_29_out, undriven, and_10_out);
  and and_30 (and_30_out, undriven_2, and_12_out);
  and and_31 (and_31_out, undriven_8, and_12_out);
  and and_32 (and_32_out, undriven_9, and_15_out);
  and and_33 (and_33_out, undriven_3, and_15_out);
  and and_34 (and_34_out, undriven_4, and_16_out);
  and and_35 (and_35_out, undriven_5, and_37_out);
  and and_36 (and_36_out, undriven_7, and_70_out);
  nor nor_8 (nor_8_out, _2, _1);
  and and_37 (and_37_out, nor_8_out, and_53_out);
  or or_80 (or_80_out, and_212_out, and_214_out, and_215_out, and_217_out);
  or or_81 (or_81_out, and_211_out, and_213_out, and_216_out, and_217_out);
  and and_38 (and_38_out, or_80_out, and_2_out);
  and and_39 (and_39_out, or_81_out, and_2_out);
  and and_40 (and_40_out, or_101_out, and_4_out);
  and and_41 (and_41_out, or_119_out, and_6_out);
  and and_42 (and_42_out, or_121_out, and_6_out);
  and and_43 (and_43_out, or_141_out, and_8_out);
  and and_44 (and_44_out, or_139_out, and_8_out);
  and and_45 (and_45_out, undriven_12, and_10_out);
  and and_46 (and_46_out, undriven_14, and_12_out);
  and and_47 (and_47_out, undriven_15, and_15_out);
  and and_48 (and_48_out, undriven_10, and_16_out);
  and and_49 (and_49_out, undriven_16, and_16_out);
  and and_50 (and_50_out, undriven_11, and_37_out);
  and and_51 (and_51_out, undriven_17, and_37_out);
  and and_52 (and_52_out, undriven_13, and_70_out);
  and and_53 (and_53_out, _3, _0);
  or or_82 (or_82_out, and_212_out, and_213_out, and_215_out, and_217_out);
  and and_54 (and_54_out, or_82_out, and_2_out);
  and and_55 (and_55_out, or_102_out, and_4_out);
  and and_56 (and_56_out, or_100_out, and_4_out);
  and and_57 (and_57_out, or_120_out, and_6_out);
  and and_58 (and_58_out, or_123_out, and_6_out);
  and and_59 (and_59_out, or_140_out, and_8_out);
  and and_60 (and_60_out, undriven_24, and_10_out);
  and and_61 (and_61_out, undriven_18, and_10_out);
  and and_62 (and_62_out, undriven_20, and_12_out);
  and and_63 (and_63_out, undriven_26, and_12_out);
  and and_64 (and_64_out, undriven_27, and_15_out);
  and and_65 (and_65_out, undriven_21, and_15_out);
  and and_66 (and_66_out, undriven_22, and_16_out);
  and and_67 (and_67_out, undriven_23, and_37_out);
  and and_68 (and_68_out, undriven_19, and_70_out);
  and and_69 (and_69_out, undriven_25, and_70_out);
  nor nor_9 (nor_9_out, _2, _0);
  and and_70 (and_70_out, nor_9_out, and_87_out);
  or or_83 (or_83_out, and_211_out, and_213_out, and_215_out, and_217_out);
  or or_84 (or_84_out, and_211_out, and_214_out, and_215_out, and_217_out);
  and and_71 (and_71_out, or_84_out, and_2_out);
  and and_72 (and_72_out, or_83_out, and_2_out);
  and and_73 (and_73_out, or_103_out, and_4_out);
  and and_74 (and_74_out, or_122_out, and_6_out);
  and and_75 (and_75_out, or_142_out, and_8_out);
  and and_76 (and_76_out, or_143_out, and_8_out);
  and and_77 (and_77_out, undriven_30, and_10_out);
  and and_78 (and_78_out, undriven_36, and_10_out);
  and and_79 (and_79_out, undriven_32, and_12_out);
  and and_80 (and_80_out, undriven_33, and_15_out);
  and and_81 (and_81_out, undriven_28, and_16_out);
  and and_82 (and_82_out, undriven_34, and_16_out);
  and and_83 (and_83_out, undriven_29, and_37_out);
  and and_84 (and_84_out, undriven_35, and_37_out);
  and and_85 (and_85_out, undriven_31, and_70_out);
  and and_86 (and_86_out, undriven_37, and_70_out);
  and and_87 (and_87_out, _3, _1);
  or or_85 (or_85_out, and_211_out, and_214_out, and_215_out, and_217_out);
  or or_86 (or_86_out, and_211_out, and_213_out, and_215_out, and_217_out);
  and and_88 (and_88_out, or_85_out, and_2_out);
  and and_89 (and_89_out, or_105_out, and_4_out);
  and and_90 (and_90_out, or_104_out, and_4_out);
  and and_91 (and_91_out, or_126_out, and_6_out);
  and and_92 (and_92_out, or_124_out, and_6_out);
  and and_93 (and_93_out, or_144_out, and_8_out);
  and and_94 (and_94_out, or_146_out, and_8_out);
  and and_95 (and_95_out, undriven_42, and_10_out);
  and and_96 (and_96_out, undriven_38, and_12_out);
  and and_97 (and_97_out, undriven_44, and_12_out);
  and and_98 (and_98_out, undriven_45, and_15_out);
  and and_99 (and_99_out, undriven_39, and_15_out);
  and and_100 (and_100_out, undriven_46, and_16_out);
  and and_101 (and_101_out, undriven_40, and_16_out);
  and and_102 (and_102_out, undriven_41, and_37_out);
  and and_103 (and_103_out, undriven_43, and_70_out);
  or or_87 (or_87_out, and_211_out, and_214_out, and_216_out, and_217_out);
  and and_104 (and_104_out, or_87_out, and_2_out);
  and and_105 (and_105_out, or_86_out, and_2_out);
  and and_106 (and_106_out, or_107_out, and_4_out);
  and and_107 (and_107_out, or_106_out, and_4_out);
  and and_108 (and_108_out, or_125_out, and_6_out);
  and and_109 (and_109_out, or_145_out, and_8_out);
  and and_110 (and_110_out, undriven_48, and_10_out);
  and and_111 (and_111_out, undriven_54, and_10_out);
  and and_112 (and_112_out, undriven_56, and_12_out);
  and and_113 (and_113_out, undriven_50, and_12_out);
  and and_114 (and_114_out, undriven_51, and_15_out);
  and and_115 (and_115_out, undriven_57, and_15_out);
  and and_116 (and_116_out, undriven_52, and_16_out);
  and and_117 (and_117_out, undriven_53, and_37_out);
  and and_118 (and_118_out, undriven_47, and_37_out);
  and and_119 (and_119_out, undriven_55, and_70_out);
  and and_120 (and_120_out, undriven_49, and_70_out);
  or or_88 (or_88_out, and_211_out, and_214_out, and_215_out, and_217_out);
  or or_89 (or_89_out, and_212_out, and_213_out, and_216_out, and_217_out);
  and and_121 (and_121_out, or_88_out, and_2_out);
  and and_122 (and_122_out, or_89_out, and_2_out);
  and and_123 (and_123_out, or_108_out, and_4_out);
  and and_124 (and_124_out, or_128_out, and_6_out);
  and and_125 (and_125_out, or_127_out, and_6_out);
  and and_126 (and_126_out, or_147_out, and_8_out);
  and and_127 (and_127_out, or_148_out, and_8_out);
  and and_128 (and_128_out, undriven_60, and_10_out);
  and and_129 (and_129_out, undriven_62, and_12_out);
  and and_130 (and_130_out, undriven_63, and_15_out);
  and and_131 (and_131_out, undriven_58, and_16_out);
  and and_132 (and_132_out, undriven_64, and_16_out);
  and and_133 (and_133_out, undriven_59, and_37_out);
  and and_134 (and_134_out, undriven_65, and_37_out);
  and and_135 (and_135_out, undriven_61, and_70_out);
  or or_90 (or_90_out, and_212_out, and_213_out, and_215_out, and_217_out);
  and and_136 (and_136_out, or_90_out, and_2_out);
  and and_137 (and_137_out, or_109_out, and_4_out);
  and and_138 (and_138_out, or_110_out, and_4_out);
  and and_139 (and_139_out, or_131_out, and_6_out);
  and and_140 (and_140_out, or_129_out, and_6_out);
  and and_141 (and_141_out, or_149_out, and_8_out);
  and and_142 (and_142_out, undriven_66, and_10_out);
  and and_143 (and_143_out, undriven_72, and_10_out);
  and and_144 (and_144_out, undriven_68, and_12_out);
  and and_145 (and_145_out, undriven_74, and_12_out);
  and and_146 (and_146_out, undriven_75, and_15_out);
  and and_147 (and_147_out, undriven_69, and_15_out);
  and and_148 (and_148_out, undriven_70, and_16_out);
  and and_149 (and_149_out, undriven_71, and_37_out);
  and and_150 (and_150_out, undriven_67, and_70_out);
  and and_151 (and_151_out, undriven_73, and_70_out);
  or or_91 (or_91_out, and_211_out, and_213_out, and_215_out, and_217_out);
  or or_92 (or_92_out, and_211_out, and_213_out, and_215_out, and_217_out);
  and and_152 (and_152_out, or_91_out, and_2_out);
  and and_153 (and_153_out, or_92_out, and_2_out);
  and and_154 (and_154_out, or_112_out, and_4_out);
  and and_155 (and_155_out, or_130_out, and_6_out);
  and and_156 (and_156_out, or_150_out, and_8_out);
  and and_157 (and_157_out, or_151_out, and_8_out);
  and and_158 (and_158_out, undriven_78, and_10_out);
  and and_159 (and_159_out, undriven_84, and_10_out);
  and and_160 (and_160_out, undriven_80, and_12_out);
  and and_161 (and_161_out, undriven_81, and_15_out);
  and and_162 (and_162_out, undriven_76, and_16_out);
  and and_163 (and_163_out, undriven_82, and_16_out);
  and and_164 (and_164_out, undriven_77, and_37_out);
  and and_165 (and_165_out, undriven_83, and_37_out);
  and and_166 (and_166_out, undriven_85, and_70_out);
  and and_167 (and_167_out, undriven_79, and_70_out);
  or or_93 (or_93_out, and_211_out, and_213_out, and_215_out, and_217_out);
  or or_94 (or_94_out, and_211_out, and_214_out, and_215_out, and_217_out);
  and and_168 (and_168_out, or_94_out, and_2_out);
  and and_169 (and_169_out, or_111_out, and_4_out);
  and and_170 (and_170_out, or_114_out, and_4_out);
  and and_171 (and_171_out, or_132_out, and_6_out);
  and and_172 (and_172_out, or_133_out, and_6_out);
  and and_173 (and_173_out, or_153_out, and_8_out);
  and and_174 (and_174_out, or_152_out, and_8_out);
  and and_175 (and_175_out, undriven_90, and_10_out);
  and and_176 (and_176_out, undriven_92, and_12_out);
  and and_177 (and_177_out, undriven_86, and_12_out);
  and and_178 (and_178_out, undriven_87, and_15_out);
  and and_179 (and_179_out, undriven_93, and_15_out);
  and and_180 (and_180_out, undriven_94, and_16_out);
  and and_181 (and_181_out, undriven_88, and_16_out);
  and and_182 (and_182_out, undriven_89, and_37_out);
  and and_183 (and_183_out, undriven_91, and_70_out);
  or or_95 (or_95_out, and_211_out, and_213_out, and_215_out, and_217_out);
  and and_184 (and_184_out, or_95_out, and_2_out);
  and and_185 (and_185_out, or_93_out, and_2_out);
  and and_186 (and_186_out, or_115_out, and_4_out);
  and and_187 (and_187_out, or_113_out, and_4_out);
  and and_188 (and_188_out, or_134_out, and_6_out);
  and and_189 (and_189_out, or_154_out, and_8_out);
  and and_190 (and_190_out, undriven_96, and_10_out);
  and and_191 (and_191_out, undriven_102, and_10_out);
  and and_192 (and_192_out, undriven_98, and_12_out);
  and and_193 (and_193_out, undriven_104, and_12_out);
  and and_194 (and_194_out, undriven_99, and_15_out);
  and and_195 (and_195_out, undriven_105, and_15_out);
  and and_196 (and_196_out, undriven_100, and_16_out);
  and and_197 (and_197_out, undriven_95, and_37_out);
  and and_198 (and_198_out, undriven_101, and_37_out);
  and and_199 (and_199_out, undriven_97, and_70_out);
  and and_200 (and_200_out, undriven_103, and_70_out);
  and and_201 (and_201_out, or_135_out, and_6_out);
  and and_202 (and_202_out, or_155_out, and_8_out);
  and and_203 (and_203_out, undriven_108, and_10_out);
  and and_204 (and_204_out, undriven_110, and_12_out);
  and and_205 (and_205_out, undriven_111, and_15_out);
  and and_206 (and_206_out, undriven_112, and_16_out);
  and and_207 (and_207_out, undriven_106, and_16_out);
  and and_208 (and_208_out, undriven_113, and_37_out);
  and and_209 (and_209_out, undriven_107, and_37_out);
  and and_210 (and_210_out, undriven_109, and_70_out);
  and and_211 (and_211_out, d_ff_1_q, nand_1_out);
  and and_212 (and_212_out, d_ff_1_q, and_220_out);
  and and_213 (and_213_out, d_ff_2_q, nand_2_out);
  and and_214 (and_214_out, d_ff_2_q, and_221_out);
  and and_215 (and_215_out, d_ff_3_q, nand_3_out);
  and and_216 (and_216_out, d_ff_3_q, and_222_out);
  and and_217 (and_217_out, or_96_out, nand_4_out);
  and and_218 (and_218_out, or_96_out, and_223_out);
  and and_219 (and_219_out, undriven_114, and_70_out);
  nand nand_1 (nand_1_out, 1'b1, d_ff_1_q);
  nand nand_2 (nand_2_out, 1'b1, d_ff_2_q);
  nand nand_3 (nand_3_out, 1'b1, d_ff_3_q);
  nand nand_4 (nand_4_out, 1'b1, or_96_out);
  and and_220 (and_220_out, 1'b1, d_ff_1_q);
  and and_221 (and_221_out, 1'b1, d_ff_2_q);
  and and_222 (and_222_out, 1'b1, d_ff_3_q);
  and and_223 (and_223_out, 1'b1, or_96_out);
  or or_96 (or_96_out, d_ff_4_q, d_ff_5_q);
  or or_97 (or_97_out, and_224_out, and_226_out, and_229_out, and_230_out);
  or or_98 (or_98_out, and_224_out, and_226_out, and_228_out, and_231_out);
  or or_99 (or_99_out, and_225_out, and_226_out, and_229_out, and_230_out);
  or or_100 (or_100_out, and_225_out, and_227_out, and_228_out, and_230_out);
  or or_101 (or_101_out, and_224_out, and_226_out, and_229_out, and_230_out);
  or or_102 (or_102_out, and_225_out, and_226_out, and_228_out, and_230_out);
  or or_103 (or_103_out, and_224_out, and_227_out, and_228_out, and_230_out);
  or or_104 (or_104_out, and_224_out, and_226_out, and_228_out, and_230_out);
  or or_105 (or_105_out, and_224_out, and_227_out, and_228_out, and_230_out);
  or or_106 (or_106_out, and_224_out, and_226_out, and_228_out, and_230_out);
  or or_107 (or_107_out, and_224_out, and_227_out, and_229_out, and_230_out);
  or or_108 (or_108_out, and_224_out, and_227_out, and_228_out, and_230_out);
  or or_109 (or_109_out, and_225_out, and_226_out, and_229_out, and_230_out);
  or or_110 (or_110_out, and_225_out, and_226_out, and_228_out, and_230_out);
  or or_111 (or_111_out, and_224_out, and_226_out, and_228_out, and_230_out);
  or or_112 (or_112_out, and_224_out, and_227_out, and_228_out, and_230_out);
  or or_113 (or_113_out, and_224_out, and_226_out, and_228_out, and_230_out);
  or or_114 (or_114_out, and_224_out, and_227_out, and_228_out, and_230_out);
  or or_115 (or_115_out, and_224_out, and_226_out, and_228_out, and_230_out);
  and and_224 (and_224_out, d_ff_1_q, nand_5_out);
  and and_225 (and_225_out, d_ff_1_q, and_232_out);
  and and_226 (and_226_out, d_ff_2_q, nand_6_out);
  and and_227 (and_227_out, d_ff_2_q, and_233_out);
  and and_228 (and_228_out, d_ff_3_q, nand_7_out);
  and and_229 (and_229_out, d_ff_3_q, and_234_out);
  and and_230 (and_230_out, or_116_out, nand_8_out);
  and and_231 (and_231_out, or_116_out, and_235_out);
  nand nand_5 (nand_5_out, 1'b1, d_ff_1_q);
  nand nand_6 (nand_6_out, 1'b1, d_ff_2_q);
  nand nand_7 (nand_7_out, 1'b1, d_ff_3_q);
  nand nand_8 (nand_8_out, 1'b1, or_116_out);
  and and_232 (and_232_out, 1'b1, d_ff_1_q);
  and and_233 (and_233_out, 1'b1, d_ff_2_q);
  and and_234 (and_234_out, 1'b1, d_ff_3_q);
  and and_235 (and_235_out, 1'b1, or_116_out);
  or or_116 (or_116_out, d_ff_4_q, d_ff_5_q);
  or or_117 (or_117_out, and_236_out, and_238_out, and_241_out, and_242_out);
  or or_118 (or_118_out, and_236_out, and_238_out, and_240_out, and_243_out);
  or or_119 (or_119_out, and_237_out, and_238_out, and_241_out, and_242_out);
  or or_120 (or_120_out, and_237_out, and_239_out, and_240_out, and_242_out);
  or or_121 (or_121_out, and_236_out, and_238_out, and_241_out, and_242_out);
  or or_122 (or_122_out, and_236_out, and_239_out, and_240_out, and_242_out);
  or or_123 (or_123_out, and_237_out, and_238_out, and_240_out, and_242_out);
  or or_124 (or_124_out, and_236_out, and_238_out, and_240_out, and_242_out);
  or or_125 (or_125_out, and_236_out, and_238_out, and_240_out, and_242_out);
  or or_126 (or_126_out, and_236_out, and_239_out, and_240_out, and_242_out);
  or or_127 (or_127_out, and_236_out, and_239_out, and_241_out, and_242_out);
  or or_128 (or_128_out, and_236_out, and_239_out, and_240_out, and_242_out);
  or or_129 (or_129_out, and_237_out, and_238_out, and_241_out, and_242_out);
  or or_130 (or_130_out, and_236_out, and_239_out, and_240_out, and_242_out);
  or or_131 (or_131_out, and_237_out, and_238_out, and_240_out, and_242_out);
  or or_132 (or_132_out, and_236_out, and_239_out, and_240_out, and_242_out);
  or or_133 (or_133_out, and_236_out, and_239_out, and_240_out, and_242_out);
  or or_134 (or_134_out, and_236_out, and_238_out, and_240_out, and_242_out);
  and and_236 (and_236_out, d_ff_1_q, nand_9_out);
  and and_237 (and_237_out, d_ff_1_q, and_244_out);
  and and_238 (and_238_out, d_ff_2_q, nand_10_out);
  and and_239 (and_239_out, d_ff_2_q, and_245_out);
  and and_240 (and_240_out, d_ff_3_q, nand_11_out);
  and and_241 (and_241_out, d_ff_3_q, and_246_out);
  and and_242 (and_242_out, or_136_out, nand_12_out);
  and and_243 (and_243_out, or_136_out, and_247_out);
  or or_135 (or_135_out, and_236_out, and_238_out, and_240_out, and_242_out);
  nand nand_9 (nand_9_out, 1'b1, d_ff_1_q);
  nand nand_10 (nand_10_out, 1'b1, d_ff_2_q);
  nand nand_11 (nand_11_out, 1'b1, d_ff_3_q);
  nand nand_12 (nand_12_out, 1'b1, or_136_out);
  and and_244 (and_244_out, 1'b1, d_ff_1_q);
  and and_245 (and_245_out, 1'b1, d_ff_2_q);
  and and_246 (and_246_out, 1'b1, d_ff_3_q);
  and and_247 (and_247_out, 1'b1, or_136_out);
  or or_136 (or_136_out, d_ff_4_q, d_ff_5_q);
  or or_137 (or_137_out, and_248_out, and_250_out, and_253_out, and_254_out);
  or or_138 (or_138_out, and_248_out, and_250_out, and_252_out, and_255_out);
  or or_139 (or_139_out, and_249_out, and_250_out, and_253_out, and_254_out);
  or or_140 (or_140_out, and_249_out, and_251_out, and_252_out, and_254_out);
  or or_141 (or_141_out, and_248_out, and_250_out, and_253_out, and_254_out);
  or or_142 (or_142_out, and_249_out, and_250_out, and_252_out, and_254_out);
  or or_143 (or_143_out, and_248_out, and_251_out, and_252_out, and_254_out);
  or or_144 (or_144_out, and_248_out, and_250_out, and_252_out, and_254_out);
  or or_145 (or_145_out, and_248_out, and_250_out, and_252_out, and_254_out);
  or or_146 (or_146_out, and_248_out, and_251_out, and_252_out, and_254_out);
  or or_147 (or_147_out, and_248_out, and_251_out, and_253_out, and_254_out);
  or or_148 (or_148_out, and_248_out, and_251_out, and_252_out, and_254_out);
  or or_149 (or_149_out, and_249_out, and_250_out, and_253_out, and_254_out);
  or or_150 (or_150_out, and_249_out, and_250_out, and_252_out, and_254_out);
  or or_151 (or_151_out, and_248_out, and_250_out, and_252_out, and_254_out);
  or or_152 (or_152_out, and_248_out, and_251_out, and_252_out, and_254_out);
  or or_153 (or_153_out, and_248_out, and_251_out, and_252_out, and_254_out);
  or or_154 (or_154_out, and_248_out, and_250_out, and_252_out, and_254_out);
  and and_248 (and_248_out, d_ff_1_q, nand_13_out);
  and and_249 (and_249_out, d_ff_1_q, and_256_out);
  and and_250 (and_250_out, d_ff_2_q, nand_14_out);
  and and_251 (and_251_out, d_ff_2_q, and_257_out);
  and and_252 (and_252_out, d_ff_3_q, nand_15_out);
  and and_253 (and_253_out, d_ff_3_q, and_258_out);
  and and_254 (and_254_out, or_156_out, nand_16_out);
  and and_255 (and_255_out, or_156_out, and_259_out);
  or or_155 (or_155_out, and_248_out, and_250_out, and_252_out, and_254_out);
  and and_256 (and_256_out, 1'b1, d_ff_1_q);
  nand nand_13 (nand_13_out, 1'b1, d_ff_1_q);
  and and_257 (and_257_out, 1'b1, d_ff_2_q);
  nand nand_14 (nand_14_out, 1'b1, d_ff_2_q);
  and and_258 (and_258_out, 1'b1, d_ff_3_q);
  nand nand_15 (nand_15_out, 1'b1, d_ff_3_q);
  and and_259 (and_259_out, 1'b1, or_156_out);
  nand nand_16 (nand_16_out, 1'b1, or_156_out);
  or or_156 (or_156_out, d_ff_4_q, d_ff_5_q);

  // Notes on the sheet:
  //   код команды
  //   флаги
  //   АЛУ 2-бит 
  //   сложение
  //   вычитание
  //   сдвиг <-
  //   сдвиг ->
  //   запись в A
  //   запись в B
  //   переход при A > B
  //   переход при A < B
  //   переход при A = B
  //   Завершить программу
endmodule
